// Logisim project cpu.circ as structural Verilog: 1 circuit, main circuit main
module main (
  input  [31:0] INSTRUCTION,
  input  CLOCK,
  output [31:0] FETCH_ADDRESS,
  output [31:0] ra,
  output [31:0] sp,
  output [31:0] t0,
  output [31:0] t1,
  output [31:0] t2,
  output [31:0] s0,
  output [31:0] s1,
  output [31:0] a0
);

  wire Arithmetic_Logic_Unit_p1, Arithmetic_Logic_Unit_p3, Arithmetic_Logic_Unit_p6,
       Arithmetic_Logic_Unit_p9, DMEM_p2, DMEM_p5, DMEM_p8, DMEM_p11;
  wire [31:0] adder_1_out, PROGRAM_COUNTER;

  Adder #(.width(32)) adder_1 (.a(PROGRAM_COUNTER), .b(32'h4), .out(adder_1_out));  // open: cin, cout
  Register #(.width(32)) PC (.D(adder_1_out), .clk(CLOCK), .Q(PROGRAM_COUNTER));  // open: en, clr
  Shifter #(.width(32), .shift("lr")) shifter_1 (.in(PROGRAM_COUNTER), .\dist (5'b00010), .out(FETCH_ADDRESS));
  // regfile_main RegFile: pin names not known
  // alu Arithmetic_Logic_Unit: pin names not known; wires that end beside it: Arithmetic_Logic_Unit_p1, ra, Arithmetic_Logic_Unit_p3, Arithmetic_Logic_Unit_p3, sp, Arithmetic_Logic_Unit_p6, Arithmetic_Logic_Unit_p6, t0, Arithmetic_Logic_Unit_p9, Arithmetic_Logic_Unit_p9
  // mem_main DMEM: pin names not known; wires that end beside it: t1, DMEM_p2, DMEM_p2, t2, DMEM_p5, DMEM_p5, s0, DMEM_p8, DMEM_p8, s1, DMEM_p11, DMEM_p11, a0, Arithmetic_Logic_Unit_p1

  // Other names for the same wires on the sheet: clk = CLOCK

  // Notes on the sheet:
  //   Output
  //   Inputs/Outputs from run.circ. DO NOT MOVE THESE.
  //   Inputs
  //   It is OK to move the PC, RegFile, ALU, and MEM to wherever is most convenient for you when constructing your CPU, and to delete this text
  //   Inputs/Outputs from run.circ. DO NOT MOVE THESE.
endmodule
